# Fritzing sketch MK-I (saved by Fritzing 0.8.7b)
circuit board: 10.4267cm x 5.60912cm
breadboards: 1

parts:
  D1 = LED_BARGRAPH_10 [package=led_bargaph_10]  # not connected
  D2 = LED_BARGRAPH_10 [package=led_bargaph_10]  # not connected
  D3 = LED_BARGRAPH_10 [package=led_bargaph_10]  # not connected
  D4 = LED_BARGRAPH_10 [package=led_bargaph_10]  # not connected
  LED1 = LED - 5mm [color="Red (633nm)" package="5 mm [THT]"]  # not connected
  LED2 = LED - 5mm [color="Red (633nm)" package="5 mm [THT]"]  # not connected
  LED3 = LED - 5mm [color="Red (633nm)" package="5 mm [THT]"]  # not connected
  LED4 = LED - 5mm [color="Red (633nm)" package="5 mm [THT]"]  # not connected
  LED5 = LED - 5mm [color="Red (633nm)" package="5 mm [THT]"]  # not connected
  LED6 = LED - 5mm [color="Red (633nm)" package="5 mm [THT]"]  # not connected
  LED7 = LED - 5mm [color="Red (633nm)" package="5 mm [THT]"]  # not connected
  LED8 = LED - 5mm [color="Red (633nm)" package="5 mm [THT]"]  # not connected
  LED9 = LED - 5mm [color="Red (633nm)" package="5 mm [THT]"]  # not connected
  LED10 = LED - 5mm [color="Red (633nm)" package="5 mm [THT]"]  # not connected
  R1 = Resistor [tolerance=±5% resistance=150 package="1206 [SMD]"]
  R2 = Resistor [tolerance=±5% resistance=150 package="1206 [SMD]"]  # not connected
  R3 = Resistor [tolerance=±5% resistance=150 package="1206 [SMD]"]  # not connected
  R4 = Resistor [tolerance=±5% resistance=150 package="1206 [SMD]"]  # not connected
  R5 = Resistor [tolerance=±5% resistance=150 package="1206 [SMD]"]  # not connected
  R6 = Resistor [tolerance=±5% resistance=150 package="1206 [SMD]"]
  R8 = Resistor [tolerance=±5% resistance=150 package="1206 [SMD]"]
  R9 = Resistor [tolerance=±5% resistance=150 package="1206 [SMD]"]
  R10 = Resistor [tolerance=±5% resistance=150 package="1206 [SMD]"]  # not connected
  S1 = Round Pushbutton  # not connected
  S2 = Round Pushbutton  # not connected
  S3 = Round Pushbutton  # not connected
  S4 = Round Pushbutton
  S5 = Round Pushbutton
  S6 = Round Pushbutton  # not connected
  S7 = Round Pushbutton
  S8 = Round Pushbutton
  S9 = Round Pushbutton  # not connected
  R11 = Rotary Potentiometer (Large) [maximum_resistance=100kΩ package=THT]
  R13 = Slide Potentiometer [maximum_resistance=100kΩ]  # not connected
  R14 = Slide Potentiometer [maximum_resistance=100kΩ]  # not connected
  Part1 = Arduino Mega 2560 (Rev3)
  R12 = Rotary Potentiometer (Large) [maximum_resistance=100kΩ package=THT]

nets:
  N1: R1.Pin_0, R6.Pin_0, R8.Pin_1, R9.Pin_0, R11.leg1, Part1.5V, R12.leg1
  N2: R1.Pin_1, S8.leg0
  N3: R6.Pin_1, S7.leg0
  N4: R8.Pin_0, S4.leg0
  N5: R9.Pin_1, S5.leg0
  N6: S4.leg1, Part1.D30
  N7: S5.leg1, Part1.D28
  N8: S7.leg1, Part1.D26
  N9: S8.leg1, Part1.D24
  N10: R11.wiper, Part1.A1
  N11: R11.leg2, Part1.GND, R12.leg2
  N12: Part1.A0, R12.wiper
